# Fritzing sketch ESP32S+Pulse+Neopixel-LED+Ultrasonic+DHT11+Display (saved by Fritzing 0.9.3b)

parts:
  U2 = ESP32S-HiLetgo [part_number=ESP32S-HiLetgo]
  Neopixel = Neopixel LED
  DHT11 = DHT11 Humitidy and Temperature Sensor (3 pins)
  SEN4 = Pulse Sensor [package=SIP-3]
  HC-SR04_Sensor_2 = HC-SR04 Ultrasonic Distance Sensor
  Grove2 = Grove OLED 128x96

nets:
  N1: U2.GPIO36, SEN4.Signal
  N2: U2.GPIO26, DHT11.DATA
  GND: U2.GND, Neopixel.Ground, DHT11.GND, SEN4.GND, HC-SR04_Sensor_2.GND, Grove2.GND
  VCC: U2.VIN, Neopixel.+5V, DHT11.VDD, SEN4.VCC, HC-SR04_Sensor_2.VCC, Grove2.VCC
  N3: U2.GPIO16, HC-SR04_Sensor_2.ECHO
  N4: U2.GPIO17, HC-SR04_Sensor_2.TRIG
  N5: U2.GPIO5, Neopixel.Data_In
  N6: U2.GPIO21, Grove2.SDA
  N7: U2.GPIO22, Grove2.SCL

notes:
  LED Flat side is on left

custom parts:
  ESP32S-HiLetgo: HiLetgo ESP-WROOM-32 ESP32 ESP-32S Development Board 2.4GHz Dual-Mode WiFi + Bluetooth Dual Cores Microcontroller The ESP32 integrated with Antenna switches, RF Balun, power amplifiers, low-noise amplifiers, filters, and management modules, and the entire solution occupies the least area of PCB. 2.4 GHz Wi-Fi plus Bluetooth dual-mode chip, with TSMC Ultra-low power consumption 40nm technology,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
  Neopixel LED: Neopixel LED 8mm (left side is flat)
  DHT11 Humitidy and Temperature Sensor (3 pins): DHT11 Humidity and Temperature Sensor (3 pins) from the design created by John De Cristofaro for Adafruit Industries.
  Pulse Sensor: Pulse Sensor Optical Heart Beat Sensor
