# Fritzing sketch dht11-esp32 (saved by Fritzing 0.9.3b)
circuit board: 8.46667cm x 5.64444cm
breadboards: 1

parts:
  U1 = ESP32S-HiLetgo [part_number=ESP32S-HiLetgo]
  DHT11 = DHT11 Humitidy and Temperature Sensor (3 pins)
  NeoPixel_LED = RGB LED (com. cathode, rbg) [package="5 mm [THT]"]

nets:
  GND: U1.GND, DHT11.GND, NeoPixel_LED.common_cathode
  VIN: U1.VIN, DHT11.VDD, NeoPixel_LED.blue_anode
  N1: U1.GPIO4, DHT11.DATA
  N2: U1.GPIO5, NeoPixel_LED.green_anode

notes:
  LED Flat side is on left

custom parts:
  ESP32S-HiLetgo: HiLetgo ESP-WROOM-32 ESP32 ESP-32S Development Board 2.4GHz Dual-Mode WiFi + Bluetooth Dual Cores Microcontroller The ESP32 integrated with Antenna switches, RF Balun, power amplifiers, low-noise amplifiers, filters, and management modules, and the entire solution occupies the least area of PCB. 2.4 GHz Wi-Fi plus Bluetooth dual-mode chip, with TSMC Ultra-low power consumption 40nm technology,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
  DHT11 Humitidy and Temperature Sensor (3 pins): DHT11 Humidity and Temperature Sensor (3 pins) from the design created by John De Cristofaro for Adafruit Industries.
